# Fritzing sketch arduinball (saved by Fritzing 0.7.4b)
breadboards: 1

parts:
  Arduino1 = Arduino
  J1 = Piezo Speaker
  R1 = Resistor [tolerance=±5% resistance=560 package=THT]
  LED1 = LED - 5mm [color="Red (633nm)" package="5 mm [THT]"]
  J2 = Basic Servo
  J3 = Infrared Proximity Sensor
  S1 = Pushbutton [package="[THT]"]
  R2 = Resistor [tolerance=±5% resistance=560 package=THT]

nets:
  N1: Arduino1.D12, LED1.anode
  N2: Arduino1.D9, J2.pulse
  N3: Arduino1.D6, J1.pin2
  N4: Arduino1.D2, S1.Pin_1, S1.Pin_2, R2.Pin_0
  N5: Arduino1.A5, J3.Vout
  GND: J1.pin1, R1.Pin_1, J2.gnd, J3.GND
  N6: R1.Pin_0, LED1.cathode
  VCC: J2.vcc, J3.Vcc
